# Fritzing sketch illumi-v0 (saved by Fritzing 0.7.1b)
breadboards: 1

parts:
  R1 = Resistor [tolerance=±5% resistance=330 package=THT]
  Composants1 = Arduino Wireless SD Shield
  LED1 = RGB LED - (4 legs) [package="5 mm [THT]"]
  R2 = Resistor [tolerance=±5% resistance=330 package=THT]
  R3 = Resistor [tolerance=±5% resistance=330 package=THT]

nets:
  N1: R1.Pin_0, LED1.red_cathode
  N2: R1.Pin_1, Composants1.D9
  N3: Composants1.+5V, LED1.common_anode
  N4: Composants1.D10, R2.Pin_1
  N5: Composants1.D11, R3.Pin_1
  N6: LED1.green_cathode, R2.Pin_0
  N7: LED1.blue_cathode, R3.Pin_0
